# Fritzing sketch Bionic Arm (saved by Fritzing 0.8.7b)
breadboards: 1

parts:
  Part1 = Arduino Nano (Rev3.0)
  R1 = Resistor [tolerance=±5% resistance=220 package=THT]
  R2 = Resistor [tolerance=±5% resistance=220 package=THT]
  R3 = Resistor [tolerance=±5% resistance=220 package=THT]
  R4 = Resistor [tolerance=±5% resistance=220 package=THT]
  R5 = Resistor [tolerance=±5% resistance=220 package=THT]
  J1 = Basic Servo
  J2 = Basic Servo
  J3 = Basic Servo
  J4 = Basic Servo
  J5 = Basic Servo
  R6 = Basic Flex Resistor
  R7 = Basic Flex Resistor
  R8 = Basic Flex Resistor
  R9 = Basic Flex Resistor
  R10 = Basic Flex Resistor
  BAT1 = BC9VPC [package=bc9vpc]

nets:
  GND: Part1.GND, J1.gnd, J2.gnd, J3.gnd, J4.gnd, J5.gnd, BAT1.V+
  N1: Part1.D2, J1.pulse
  N2: Part1.D3, J2.pulse
  N3: Part1.D4, J3.pulse
  N4: Part1.D5, J4.pulse
  N5: Part1.D8, J5.pulse
  N6: Part1.VIN, BAT1.V-
  VCC: Part1.5V, R1.Pin_0, R2.Pin_0, R3.Pin_0, R4.Pin_0, R5.Pin_0, J1.vcc, J2.vcc, J3.vcc, J4.vcc, J5.vcc, R6.pin_1, R7.pin_1, R8.pin_1, R9.pin_1, R10.pin_1
  N7: Part1.A4, R5.Pin_1, R6.Pin_2
  N8: Part1.A3, R4.Pin_1, R7.Pin_2
  N9: Part1.A2, R3.Pin_1, R8.Pin_2
  N10: Part1.A1, R2.Pin_1, R9.Pin_2
  N11: Part1.A0, R1.Pin_1, R10.Pin_2
